// Logisim project Trabalho SD final.circ as structural Verilog: 1 circuit, main circuit Complementar de Q0
module Complementar_de_Q0 (
  input  Interruptor,
  input  Sensor
);

  wire and_1_out, and_2_out, and_3_out, and_4_out, and_5_out, and_6_out, and_7_out, clock_1_out, JK_0_q,
       JK_0_qn, JK_1_q, JK_1_qn, JK_2_q, JK_2_qn, not_1_out, or_1_out, or_2_out, or_3_out, or_4_out,
       or_5_out, or_6_out;

  Clock clock_1 (.out(clock_1_out));
  not not_1 (not_1_out, Interruptor);
  and and_1 (and_1_out, JK_2_qn, Interruptor);
  and and_2 (and_2_out, JK_2_qn, JK_1_q);
  and and_3 (and_3_out, JK_2_q, JK_1_qn);
  and and_4 (and_4_out, not_1_out, Sensor, JK_2_qn);
  or or_1 (or_1_out, and_1_out, and_2_out, and_3_out);
  or or_2 (or_2_out, and_4_out, JK_0_q);
  or or_3 (or_3_out, JK_0_q, JK_2_q);
  and and_5 (and_5_out, JK_1_q, JK_0_q);
  J_K_Flip_Flop JK_0 (.J(or_1_out), .clk(clock_1_out), .K(1'b1), .Q(JK_0_q), .Qn(JK_0_qn));  // open: preset, en, reset
  J_K_Flip_Flop JK_1 (
    .J(or_2_out), .clk(clock_1_out), .K(or_3_out), .Q(JK_1_q), .Qn(JK_1_qn));  // open: preset, en, reset
  J_K_Flip_Flop JK_2 (
    .J(and_5_out), .clk(clock_1_out), .K(JK_1_q), .Q(JK_2_q), .Qn(JK_2_qn));  // open: preset, en, reset
  or or_4 (or_4_out, JK_1_qn, JK_0_q);
  _7_Segment_Display u_7_segment_display_1 (
    .g(or_5_out), .f(1'b1), .a(or_5_out), .b(or_4_out), .e(1'b1), .d(or_6_out), .c(or_4_out));  // open: dp
  and and_6 (and_6_out, JK_0_qn, JK_1_qn);
  and and_7 (and_7_out, JK_2_q, JK_1_qn);
  or or_5 (or_5_out, JK_0_q, JK_1_q, and_7_out);
  or or_6 (or_6_out, and_6_out, JK_1_q, JK_2_q);

  // Notes on the sheet:
  //   Q0
  //   Q2
  //   Q1
endmodule
